// Logisim project CPU.circ as structural Verilog: 2 circuits, main circuit main
module main (
  input  Reset,
  input  Start
);

  wire and_1_out, and_2_out, and_3_out, and_4_out, and_5_out, and_6_out, and_7_out, and_8_out, and_9_out,
       and_10_out, and_11_out, and_12_out, and_13_out, and_14_out, and_15_out, and_16_out, and_17_out,
       and_18_out, and_19_out, and_20_out, and_21_out, and_22_out, and_23_out, and_24_out, and_25_out,
       and_26_out, and_27_out, and_28_out, and_30_out, and_31_out, and_32_out, and_33_out, and_34_out,
       and_35_out, and_36_out, and_37_out, clock_1_out, comparator_1_eq, comparator_1_gt, comparator_1_lt,
       decoder_1_out0, decoder_1_out1, decoder_1_out2, decoder_1_out3, decoder_1_out4, decoder_2_out0,
       decoder_2_out1, decoder_2_out2, decoder_2_out3, decoder_3_out0, decoder_3_out1, decoder_3_out2,
       decoder_3_out3, decoder_3_out4, decoder_4_out1, decoder_4_out2, decoder_4_out3, decoder_4_out4,
       decoder_4_out5, decoder_4_out6, decoder_4_out7, decoder_4_out8, decoder_4_out9, decoder_4_out10,
       decoder_4_out11, decoder_4_out14, decoder_4_out15, keyboard_1_avail, multiplexer_1_out, not_1_out,
       not_2_out, not_3_out, not_4_out, not_5_out, not_6_out, not_7_out, not_8_out, not_9_out, or_1_out,
       or_2_out, or_3_out, or_4_out, or_5_out, or_6_out, or_7_out, or_8_out, or_9_out, or_10_out, or_11_out,
       or_12_out, or_13_out, or_14_out, register_10_q;
  wire [1:0] register_7_q_2;
  wire [3:0] counter_2_q, register_2_q, register_3_q, register_9_q, rom_1_data_2;
  wire [6:0] keyboard_1_data;
  wire [7:0] adder_1_out, alu_8bit_1_c0, controlled_buffer_1_out, controlled_buffer_8_out, counter_1_q,
       ram_1_data, register_1_q, register_4_q, register_5_q, register_6_q, register_8_q;
  wire [7:2] register_7_q;
  wire [7:4] rom_1_data;

  Clock clock_1 (.out(clock_1_out));
  not not_1 (not_1_out, or_11_out);
  and and_1 (and_1_out, clock_1_out, Start, not_1_out);
  Counter counter_1 (.Q(counter_1_q), .clk(and_1_out), .clr(or_1_out));  // open: load, D, count, carry
  or or_1 (or_1_out, and_2_out, Reset);
  and and_2 (and_2_out, or_14_out, not_2_out);
  Register register_1 (.D(controlled_buffer_1_out), .Q(register_1_q), .clk(not_2_out), .clr(Reset));  // open: en
  not not_2 (not_2_out, and_3_out);
  and and_3 (and_3_out, and_1_out, or_14_out);
  Adder adder_1 (.a(counter_1_q), .b(register_1_q), .out(adder_1_out));  // open: cin, cout
  or or_2 (or_2_out, Reset, decoder_2_out3);
  Decoder #(.select(4)) decoder_1 (
    .out0(decoder_1_out0), .out1(decoder_1_out1), .out2(decoder_1_out2), .out3(decoder_1_out3),
    .out4(decoder_1_out4), .sel(register_2_q));  // open: out5, out6, out7, out8, out9, out10, out11, out12, out13, out14, out15, en
  Register #(.width(4)) register_2 (.D(rom_1_data_2), .Q(register_2_q), .clk(not_5_out), .clr(Reset));  // open: en
  Counter #(.width(4), .max('hf)) counter_2 (
    .Q(counter_2_q), .clk(and_1_out), .clr(or_2_out));  // open: load, D, count, carry
  assign controlled_buffer_1_out = or_6_out ? {rom_1_data, rom_1_data_2} : 8'bz;  // Controlled_Buffer controlled_buffer_1
  Decoder #(.select(4)) decoder_2 (
    .out0(decoder_2_out0), .out1(decoder_2_out1), .out2(decoder_2_out2), .out3(decoder_2_out3),
    .sel(counter_2_q));  // open: out4, out5, out6, out7, out8, out9, out10, out11, out12, out13, out14, out15, en
  ROM rom_1 (.addr(adder_1_out), .data({rom_1_data, rom_1_data_2}));  // open: sel
  Register #(.width(4)) register_3 (.D(rom_1_data_2), .Q(register_3_q), .clk(not_4_out), .clr(Reset));  // open: en
  Decoder #(.select(4)) decoder_3 (
    .out0(decoder_3_out0), .out1(decoder_3_out1), .out2(decoder_3_out2), .out3(decoder_3_out3),
    .out4(decoder_3_out4), .sel(register_3_q));  // open: out5, out6, out7, out8, out9, out10, out11, out12, out13, out14, out15, en
  assign controlled_buffer_1_out = and_5_out ? register_4_q : 8'bz;  // Controlled_Buffer controlled_buffer_2
  Register register_4 (.D(controlled_buffer_1_out), .Q(register_4_q), .clk(and_4_out), .clr(Reset));  // open: en
  and and_4 (and_4_out, decoder_1_out0, or_5_out);
  and and_5 (and_5_out, or_4_out, decoder_3_out0);
  assign controlled_buffer_1_out = and_6_out ? register_5_q : 8'bz;  // Controlled_Buffer controlled_buffer_3
  Register register_5 (.D(controlled_buffer_1_out), .Q(register_5_q), .clk(and_7_out), .clr(Reset));  // open: en
  and and_6 (and_6_out, or_4_out, decoder_3_out1);
  and and_7 (and_7_out, decoder_1_out1, or_5_out);
  assign controlled_buffer_1_out = and_9_out ? register_6_q : 8'bz;  // Controlled_Buffer controlled_buffer_4
  Register register_6 (.D(controlled_buffer_1_out), .Q(register_6_q), .clk(and_8_out), .clr(Reset));  // open: en
  and and_8 (and_8_out, decoder_1_out2, or_5_out);
  and and_9 (and_9_out, or_4_out, decoder_3_out2);
  assign controlled_buffer_1_out = and_10_out ? {register_7_q, register_7_q_2} : 8'bz;  // Controlled_Buffer controlled_buffer_5
  Register register_7 (
    .D(controlled_buffer_1_out), .Q({register_7_q, register_7_q_2}), .clk(or_3_out), .clr(Reset));  // open: en
  or or_3 (or_3_out, and_11_out, and_30_out);
  and and_10 (and_10_out, or_4_out, decoder_3_out3);
  and and_11 (and_11_out, decoder_1_out3, or_5_out);
  assign controlled_buffer_1_out = and_13_out ? register_8_q : 8'bz;  // Controlled_Buffer controlled_buffer_6
  Register register_8 (.D(controlled_buffer_1_out), .Q(register_8_q), .clk(and_12_out), .clr(Reset));  // open: en
  and and_12 (and_12_out, decoder_1_out4, or_5_out);
  and and_13 (and_13_out, or_4_out, decoder_3_out4);
  Register #(.width(4)) register_9 (.D(rom_1_data_2), .Q(register_9_q), .clk(not_3_out), .clr(Reset));  // open: en
  not not_3 (not_3_out, decoder_2_out0);
  and and_14 (and_14_out, or_7_out, and_1_out);
  not not_4 (not_4_out, and_14_out);
  not not_5 (not_5_out, and_15_out);
  and and_15 (and_15_out, and_1_out, or_8_out);
  and and_16 (and_16_out, or_9_out, and_1_out);
  or or_4 (or_4_out, and_36_out, and_16_out);
  and and_17 (and_17_out, and_1_out, or_10_out);
  or or_5 (or_5_out, and_36_out, and_17_out);
  buf or_6 (or_6_out, and_20_out);  // OR_Gate
  or or_7 (or_7_out, and_23_out, and_26_out, and_34_out, and_35_out);
  or or_8 (or_8_out, and_19_out, and_27_out, and_31_out, and_36_out);
  or or_9 (or_9_out, and_22_out, and_25_out, and_33_out);
  or or_10 (or_10_out, and_20_out, and_21_out, and_32_out);
  Comparator comparator_1 (
    .a(register_5_q), .b(register_6_q), .gt(comparator_1_gt), .eq(comparator_1_eq), .lt(comparator_1_lt));
  assign controlled_buffer_1_out = and_30_out ? alu_8bit_1_c0 : 8'bz;  // Controlled_Buffer controlled_buffer_7
  Multiplexer #(.select(2)) multiplexer_1 (
    .in0(comparator_1_gt), .in1(comparator_1_eq), .in2(comparator_1_lt), .out(multiplexer_1_out),
    .sel(register_7_q_2));  // open: in3, en
  and and_18 (and_18_out, not_9_out, decoder_4_out11);
  Decoder #(.select(4)) decoder_4 (
    .out1(decoder_4_out1), .out2(decoder_4_out2), .out3(decoder_4_out3), .out4(decoder_4_out4),
    .out5(decoder_4_out5), .out6(decoder_4_out6), .out7(decoder_4_out7), .out8(decoder_4_out8),
    .out9(decoder_4_out9), .out10(decoder_4_out10), .out11(decoder_4_out11), .out14(decoder_4_out14),
    .out15(decoder_4_out15), .sel(register_9_q));  // open: out0, out12, out13, en
  and and_19 (and_19_out, decoder_2_out1, decoder_4_out14);
  and and_20 (and_20_out, decoder_2_out2, decoder_4_out14);
  not not_6 (not_6_out, and_28_out);
  ALU_8bit alu_8bit_1 (
    .A0(register_5_q[0]), .A1(register_5_q[1]), .A2(register_5_q[2]), .A3(register_5_q[3]),
    .A4(register_5_q[4]), .A5(register_5_q[5]), .A6(register_5_q[6]), .A7(register_5_q[7]),
    .B0(register_6_q[0]), .B1(register_6_q[1]), .B2(register_6_q[2]), .B3(register_6_q[3]),
    .B4(register_6_q[4]), .B5(register_6_q[5]), .B6(register_6_q[6]), .B7(register_6_q[7]),
    .O0(register_4_q[0]), .O1(register_4_q[1]), .O2(register_4_q[2]), .O3(register_4_q[3]),
    .C0(alu_8bit_1_c0[0]), .C1(alu_8bit_1_c0[1]), .C2(alu_8bit_1_c0[2]), .C3(alu_8bit_1_c0[3]),
    .C4(alu_8bit_1_c0[4]), .C5(alu_8bit_1_c0[5]), .C6(alu_8bit_1_c0[6]), .C7(alu_8bit_1_c0[7]));
  assign controlled_buffer_8_out = and_33_out ? controlled_buffer_1_out : 8'bz;  // Controlled_Buffer controlled_buffer_8
  assign controlled_buffer_1_out = and_32_out ? {1'b0, keyboard_1_data} : 8'bz;  // Controlled_Buffer controlled_buffer_9
  Register #(.width(1)) register_10 (
    .D(multiplexer_1_out), .Q(register_10_q), .clk(and_18_out), .clr(Reset));  // open: en
  and and_21 (and_21_out, decoder_2_out2, decoder_4_out2);
  and and_22 (and_22_out, decoder_2_out2, decoder_4_out1);
  and and_23 (and_23_out, decoder_2_out1, decoder_4_out1);
  RAM #(.bus("separate")) ram_1 (
    .addr(register_8_q), .din(controlled_buffer_1_out), .data(ram_1_data), .clk(not_6_out), .clr(Reset));  // open: str, sel, ld
  TTY #(.rows(15)) tty_1 (.data(controlled_buffer_8_out[6:0]), .clk(and_37_out), .clr(Reset));  // open: we
  or or_11 (or_11_out, decoder_4_out15, and_24_out);
  and and_24 (and_24_out, and_31_out, not_7_out);
  not not_7 (not_7_out, keyboard_1_avail);
  and and_25 (and_25_out, decoder_2_out2, register_10_q, decoder_4_out3);
  and and_26 (and_26_out, decoder_2_out1, register_10_q, decoder_4_out3);
  and and_27 (and_27_out, decoder_2_out1, decoder_4_out2);
  buf or_12 (or_12_out, and_22_out);  // OR_Gate
  and and_28 (and_28_out, and_1_out, or_12_out);
  Keyboard keyboard_1 (.clk(not_8_out), .clr(Reset), .avail(keyboard_1_avail), .data(keyboard_1_data));  // open: re
  // AND_Gate and_29 has open pins: in0=decoder_2_out1, in1=decoder_4_out4, out=open
  and and_30 (and_30_out, decoder_2_out2, decoder_4_out4);
  buf or_13 (or_13_out, and_21_out);  // OR_Gate
  assign controlled_buffer_1_out = or_13_out ? ram_1_data : 8'bz;  // Controlled_Buffer controlled_buffer_10
  not not_8 (not_8_out, and_32_out);
  and and_31 (and_31_out, decoder_2_out1, decoder_4_out5);
  and and_32 (and_32_out, decoder_2_out2, decoder_4_out5);
  and and_33 (and_33_out, decoder_2_out2, decoder_4_out6);
  buf or_14 (or_14_out, and_25_out);  // OR_Gate
  and and_34 (and_34_out, decoder_2_out1, decoder_4_out6);
  and and_35 (and_35_out, decoder_2_out1, decoder_4_out7);
  and and_36 (and_36_out, decoder_2_out2, decoder_4_out7);
  not not_9 (not_9_out, and_1_out);
  and and_37 (and_37_out, and_33_out, not_9_out);
  // AND_Gate and_38 has open pins: in0=decoder_2_out2, in1=decoder_4_out8, out=open
  // AND_Gate and_39 has open pins: in0=decoder_2_out1, in1=decoder_4_out8, out=open
  // AND_Gate and_40 has open pins: in0=decoder_2_out2, in1=decoder_4_out10, out=open
  // AND_Gate and_41 has open pins: in0=decoder_2_out1, in1=decoder_4_out9, out=open
  // AND_Gate and_42 has open pins: in0=decoder_2_out2, in1=decoder_4_out9, out=open
  // AND_Gate and_43 has open pins: in0=decoder_2_out1, in1=decoder_4_out10, out=open

  // Notes on the sheet:
  //   BIOS
  //   GET
  //   contents of rom_1 (hex, n*v repeats v):
  //   e 0 57 6 0 0 e 0 70 6 0 0 e 0 72 6 0 0 e 0 6f 6 0 0 e 0 77 6 0 0 e 0 61 6 0 0 e 0 64 6 0 0 e 0 7a 6
  //   0 0 e 0 69 6 0 0 5 1 0 e 2 31 e 3 1 b 0 0 e 0 54 3 0 0 e 0 d 6 0 0 e 0 41 6 0 0 f
  //   R0
  //   R1
  //   R2
  //   R3
  //   R4
  //   PUT
  //   Compare
  //   RAM
  //   ALU
  //   Decoder
  //   Keyboard
  //   Terminal
endmodule

module ALU_8bit (
  input  O0,
  input  O1,
  input  A0,
  input  O2,
  input  A1,
  input  O3,
  input  A2,
  input  A3,
  input  A4,
  input  A5,
  input  A6,
  input  A7,
  input  B0,
  input  B1,
  input  B2,
  input  B3,
  input  B4,
  input  B5,
  input  B6,
  input  B7,
  output C0,
  output C1,
  output C2,
  output C3,
  output C4,
  output C5,
  output C6,
  output C7
);

  wire [7:0] adder_1_out, and_1_out, divider_1_out, multiplier_1_out, nand_1_out, nor_1_out, not_1_out,
       or_1_out, subtractor_1_out, xor_1_out;

  assign and_1_out = {A7, A6, A5, A4, A3, A2, A1, A0} & {B7, B6, B5, B4, B3, B2, B1, B0};  // AND_Gate and_1, 8 bits wide
  assign or_1_out = {A7, A6, A5, A4, A3, A2, A1, A0} | {B7, B6, B5, B4, B3, B2, B1, B0};  // OR_Gate or_1, 8 bits wide
  assign xor_1_out = {A7, A6, A5, A4, A3, A2, A1, A0} ^ {B7, B6, B5, B4, B3, B2, B1, B0};  // XOR_Gate xor_1, 8 bits wide
  assign nand_1_out = ~({A7, A6, A5, A4, A3, A2, A1, A0} & {B7, B6, B5, B4, B3, B2, B1, B0});  // NAND_Gate nand_1, 8 bits wide
  assign nor_1_out = ~({A7, A6, A5, A4, A3, A2, A1, A0} | {B7, B6, B5, B4, B3, B2, B1, B0});  // NOR_Gate nor_1, 8 bits wide
  Adder adder_1 (
    .a({A7, A6, A5, A4, A3, A2, A1, A0}), .b({B7, B6, B5, B4, B3, B2, B1, B0}), .out(adder_1_out));  // open: cin, cout
  Subtractor subtractor_1 (
    .a({A7, A6, A5, A4, A3, A2, A1, A0}), .b({B7, B6, B5, B4, B3, B2, B1, B0}), .out(subtractor_1_out));  // open: bin, bout
  Multiplier multiplier_1 (
    .a({A7, A6, A5, A4, A3, A2, A1, A0}), .b({B7, B6, B5, B4, B3, B2, B1, B0}), .out(multiplier_1_out));  // open: cin, cout
  Divider divider_1 (
    .a({A7, A6, A5, A4, A3, A2, A1, A0}), .b({B7, B6, B5, B4, B3, B2, B1, B0}), .out(divider_1_out));  // open: upper, rem
  assign not_1_out = ~{A7, A6, A5, A4, A3, A2, A1, A0};  // NOT_Gate not_1, 8 bits wide
  Multiplexer #(.select(4), .width(8)) multiplexer_1 (
    .in0({A7, A6, A5, A4, A3, A2, A1, A0}), .in1(not_1_out), .in2(and_1_out), .in3(or_1_out),
    .in4(xor_1_out), .in5(nand_1_out), .in6(nor_1_out), .in7({8{1'b1}}), .in8({8{1'b0}}), .in9(adder_1_out),
    .in10(subtractor_1_out), .in11(multiplier_1_out), .in12(divider_1_out),
    .out({C7, C6, C5, C4, C3, C2, C1, C0}), .sel({O3, O2, O1, O0}));  // open: in13, in14, in15, en
endmodule
